# Fritzing sketch design-max30205 (saved by Fritzing 0.9.6b)
breadboards: 1

parts:
  Mod1 = Raspberry Pi 4B
  R1 = Resistor [tolerance=±5% power=0.25 resistance=4.7k package=THT]
  C1 = Electrolytic Capacitor [capacitance=1μF voltage=35V package="0405 [SMD, electrolytic]"]
  M1 = Max30205 body temp sensor [package=THT]
  R2 = Resistor [tolerance=±5% power=0.25 resistance=4.7k package=THT]
  R3 = Resistor [tolerance=±5% power=0.25 resistance=4.7k package=THT]

nets:
  3V3: Mod1.3V3, R1.Pin_0, C1.+, M1.VCC, R2.Pin_0, R3.Pin_1
  N1: Mod1.GPIO2, R1.Pin_1, M1.SDA
  N2: Mod1.GPIO3, M1.SCL, R2.Pin_1
  GND: Mod1.GND, C1.-, M1.GND, M1.A0, M1.A1, M1.A2
  N3: M1.OS, R3.Pin_0

custom parts:
  Max30205 body temp sensor: This module is based on MAX30205 which is a temperature sensor that accurately measures temperature and provides an over-temperature alarm/interrupt/shutdown output.
