# Fritzing sketch design-combined (saved by Fritzing 0.9.6b)
breadboards: 2

parts:
  Mod1 = Raspberry Pi 4B
  R1 = Resistor [tolerance=±5% power=0.25 resistance=4.7k package=THT]
  C1 = Electrolytic Capacitor [capacitance=1μF voltage=35V package="0405 [SMD, electrolytic]"]
  M1 = Max30205 body temp sensor [package=THT]
  R2 = Resistor [tolerance=±5% power=0.25 resistance=4.7k package=THT]
  R3 = Resistor [tolerance=±5% power=0.25 resistance=4.7k package=THT]
  MAX30102_Sensor2 = MAX30102 Oximeter and Heart-Rate Sensor [part_number=MAX30102]  # not connected
  Mod3 = AD8232 HeartRate Monitor [part_number=SEN-12650]
  Part2 = Adafruit ADS1115 16Bit I2C ADC [part_number="Adafruit #1085"]
  R4 = Resistor [tolerance=±5% resistance=10k package="0603 [SMD]"]
  LED2 = smd LED [color="Red (633nm)" package="0603 [SMD]"]
  R5 = Resistor [tolerance=±5% resistance=330 package="2512 [SMD]"]
  RHT3 = Humidity and Temperature Sensor RHT03

nets:
  VCC: Mod1.3V3, R1.Pin_0, C1.+, M1.VCC, M1.A0, R2.Pin_0, R3.Pin_1, Mod3.3.3v, Part2.VDD, R4.Pin_0, RHT3.Vcc
  N1: Mod1.GPIO2, R1.Pin_1, M1.SDA, Part2.SDA
  N2: Mod1.GPIO3, M1.SCL, R2.Pin_1, Part2.SCL
  GND: Mod1.GND, C1.-, M1.GND, M1.A1, M1.A2, Mod3.GND, Part2.ALERT, Part2.GND, R5.Pin_0, RHT3.GND_2
  N3: Mod1.GPIO17, R4.Pin_1, RHT3.Data-signal
  N4: Mod1.GPIO18, LED2.anode
  N5: Mod1.GPIO27, Part2.ADDR
  N6: M1.OS, R3.Pin_0
  N7: Mod3.OUTPUT, Part2.AIN0
  N8: LED2.cathode, R5.Pin_1

custom parts:
  Max30205 body temp sensor: This module is based on MAX30205 which is a temperature sensor that accurately measures temperature and provides an over-temperature alarm/interrupt/shutdown output.
  MAX30102 Oximeter and Heart-Rate Sensor: The MAX30102 is an integrated pulse oximetry and heart-rate monitor biosensor module. It includes internal LEDs, photodetectors, optical elements, and low-noise electronics with ambient light rejection. The MAX30102 operates on a single 1.8V power supply and a separate 3.3V power supply for the internal LEDs. Communication is through a I2C-compatible interface.
  AD8232 HeartRate Monitor: Sparkfun single lead heart rate monitor - Ad8232.
  Adafruit ADS1115 16Bit I2C ADC: For microcontrollers without an analog-to-digital converter or when you want a higher-precision ADC, the ADS1115 provides 16-bit precision at 860 samples/second over I2C. The chip can be configured as 4 single-ended input channels, or two differential channels. As a nice bonus, it even includes a programmable gain amplifier, up to x16, to help boost up smaller single/differential signals to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
