# Fritzing sketch design-ad8232 (saved by Fritzing 0.9.6b)
breadboards: 1

parts:
  Mod1 = Raspberry Pi 4B
  Mod2 = AD8232 HeartRate Monitor [part_number=SEN-12650]
  Part1 = Adafruit ADS1115 16Bit I2C ADC [part_number="Adafruit #1085"]

nets:
  3V3: Mod1.3V3, Mod2.3.3v, Part1.VDD
  N1: Mod1.GPIO2, Part1.SDA
  N2: Mod1.GPIO3, Part1.SCL
  GND: Mod1.GND, Mod2.GND, Part1.ALERT, Part1.GND
  N3: Mod1.GPIO27, Part1.ADDR
  N4: Mod2.OUTPUT, Part1.AIN0

custom parts:
  AD8232 HeartRate Monitor: Sparkfun single lead heart rate monitor - Ad8232.
  Adafruit ADS1115 16Bit I2C ADC: For microcontrollers without an analog-to-digital converter or when you want a higher-precision ADC, the ADS1115 provides 16-bit precision at 860 samples/second over I2C. The chip can be configured as 4 single-ended input channels, or two differential channels. As a nice bonus, it even includes a programmable gain amplifier, up to x16, to help boost up smaller single/differential signals to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
