# Fritzing sketch sketch-max30102 (saved by Fritzing 0.9.6b)
breadboards: 1

parts:
  Mod1 = Raspberry Pi 4B
  MAX30102_Sensor1 = MAX30102 Oximeter and Heart-Rate Sensor [part_number=MAX30102]

nets:
  3V3: Mod1.3V3, MAX30102_Sensor1.VIN
  N1: Mod1.GPIO2, MAX30102_Sensor1.SDA
  N2: Mod1.GPIO3, MAX30102_Sensor1.SCL
  GND: Mod1.GND, MAX30102_Sensor1.GND

custom parts:
  MAX30102 Oximeter and Heart-Rate Sensor: The MAX30102 is an integrated pulse oximetry and heart-rate monitor biosensor module. It includes internal LEDs, photodetectors, optical elements, and low-noise electronics with ambient light rejection. The MAX30102 operates on a single 1.8V power supply and a separate 3.3V power supply for the internal LEDs. Communication is through a I2C-compatible interface.
