# Fritzing sketch led (saved by Fritzing 0.9.6b)
breadboards: 1

parts:
  Mod2 = Raspberry Pi 4B
  LED1 = smd LED [color="Red (633nm)" package="0603 [SMD]"]
  R1 = Resistor [tolerance=±5% resistance=330 package="2512 [SMD]"]

nets:
  N1: Mod2.GND, R1.Pin_0
  N2: Mod2.GPIO18, LED1.anode
  N3: LED1.cathode, R1.Pin_1
