# Fritzing sketch design-bmp280 (saved by Fritzing 0.9.6b)
breadboards: 1

parts:
  Mod1 = Raspberry Pi 4B
  BMP280_Breakout1 = BMP280 Breakout Board [part_number=BMP280]

nets:
  3V3: Mod1.3V3, BMP280_Breakout1.VCC
  N1: Mod1.GPIO2, BMP280_Breakout1.SDA
  N2: Mod1.GPIO3, BMP280_Breakout1.SCL
  GND: Mod1.GND, BMP280_Breakout1.GND

custom parts:
  BMP280 Breakout Board: This is a breakout board for the Bosch Sensortec BMP280, "an absolute barometric pressure sensor especially designed for mobile applications." The operation range is 300 to 1100 hPa. Supply voltage is 1.2 to 3.6V. Operating temperature range is -40 to +85 °C.
