# Fritzing sketch sketch-arduino (saved by Fritzing 0.9.6b)
breadboards: 1

parts:
  Part1 = Arduino Uno (Rev3) - ICSP
  Part2 = Barometric Pressure Sensor - BMP180 Breakout (GY-68)

nets:
  N1: Part1.A4/SDA, Part2.SDA
  N2: Part1.A5/SCL, Part2.SCL
  5V: Part1.5V, Part2.VCC
  GND: Part1.GND, Part2.GND
