# Fritzing sketch sketch (saved by Fritzing 0.9.6b)
breadboards: 1

parts:
  RHT1 = Humidity and Temperature Sensor RHT03
  Mod1 = Raspberry Pi 4B
  R1 = Resistor [tolerance=±5% resistance=10k package="0603 [SMD]"]
  LED1 = LED - 3mm [color="Red (633nm)" current=0.030 package="3 mm [THT]"]
  R2 = Resistor [tolerance=±5% resistance=3.3 package="0603 [SMD]"]
  J1 = Piezo Speaker

nets:
  VCC: RHT1.Vcc, Mod1.3V3, R1.Pin_0
  N1: RHT1.Data-signal, Mod1.GPIO17, R1.Pin_1
  N2: RHT1.GND_2, Mod1.GND, R2.Pin_1, J1.pin1
  N3: Mod1.GPIO18, LED1.anode
  N4: Mod1.GPIO27, J1.pin2
  N5: LED1.cathode, R2.Pin_0

notes:
  10kΩ resistor for DHT22
  330Ω resistor for LED
